# Fritzing sketch Thermal_Printer_Wiring (saved by Fritzing 0.9.3b)
breadboards: 1

parts:
  Raspberry_Pi_B_rev1 = Raspberry Pi B rev1
  LED1 = smd LED [color="Green (570nm)" package="0603 [SMD]"]
  LED2 = smd LED [color="Red (633nm)" package="0603 [SMD]"]
  R1 = Resistor [tolerance=±5% resistance=220 package=THT]
  R2 = Resistor [tolerance=±5% resistance=220 package=THT]
  S1 = Round Pushbutton
  Power_plug1 = Power plug
  Part1 = Thermal Printer

nets:
  N1: Raspberry_Pi_B_rev1.3V3, S1.leg0
  N2: Raspberry_Pi_B_rev1.GND, LED1.anode, LED2.anode, Part1.GND#2
  N3: Raspberry_Pi_B_rev1.GPIO_14, Part1.RXD
  N4: Raspberry_Pi_B_rev1.GPIO_15, Part1.TXD
  N5: Raspberry_Pi_B_rev1.GPIO_24, R1.Pin_1
  N6: Raspberry_Pi_B_rev1.GPIO_25, R2.Pin_1
  N7: Raspberry_Pi_B_rev1.GPIO_11, S1.leg1
  N8: LED1.cathode, R1.Pin_0
  N9: LED2.cathode, R2.Pin_0
  N10: Power_plug1.GND, Part1.GND#0
  N11: Power_plug1.VCC, Part1.VH
